# Fritzing sketch PhaseThree (saved by Fritzing 0.9.3b)
breadboards: 1

parts:
  Part1 = Arduino Uno (Rev3)
  Pololu_A1 = Pololu A4988 [package=SO16]
  M1 = Stepper Motor - Bipolar
  U2 = LIPO-2000mAh [package=lipo-2000]
  S1 = Pushbutton [package="[THT]"]
  S2 = Pushbutton [package="[THT]"]
  R2 = Resistor [tolerance=±5% resistance=10k package="2010 [SMD]"]
  R1 = Resistor [tolerance=±5% resistance=10k package="2010 [SMD]"]
  Part2 = SO-24x [chip_label=SO-24x package=SO(x)]  # not connected
  MD03A1 = Dual VNH2SP30 Motor Driver [part_number=MD03A]  # not connected

nets:
  5V: Part1.D2, Part1.D3_PWM, Part1.5V, Pololu_A1.MS1, Pololu_A1.MS3, Pololu_A1.VDD, S1.Pin_1, S1.Pin_2, S2.Pin_1, S2.Pin_2
  N1: Part1.D4, Pololu_A1.DIR
  N2: Part1.D5_PWM, Pololu_A1.STEP
  N3: Part1.D6_PWM, Pololu_A1.ENABLE
  N4: Part1.GND, Pololu_A1.MS2, Pololu_A1.GND#8, R2.Pin_1, R1.Pin_1
  N5: Pololu_A1.RESET, Pololu_A1.SLEEP
  N6: Pololu_A1.1B, M1.A
  N7: Pololu_A1.1A, M1.C
  N8: Pololu_A1.2A, M1.B
  N9: Pololu_A1.2B, M1.D
  N10: Pololu_A1.GND#14, U2.-
  N11: Pololu_A1.VMOT, U2.+
  N12: S1.Pin_4, R2.Pin_0
  N13: S2.Pin_4, R1.Pin_0

notes:
  ExoArm Phase Two circuit
